# Fritzing sketch minimum-DRO_scheme (saved by Fritzing 0.9.5d)

parts:
  Grove1 = TM1637 7segment 4digit display
  Компонент2 = USB Mini-B Breakout [part_number=1764]
  Компонент4 = USB Mini-B Breakout [part_number=1764]  # not connected
  Matrix_keypad1 = KEYPAD 4x4
  M1 = pcf8574 io expansion board [package=THT]
  S2 = Taiway 100-SP-X-T1 SPDT Miniature Toggle Switch [part_number=100-SP-X-T1-0-0-B1-M1 package=THT]
  S4 = Round Pushbutton
  U1 = Mini-360 DC-DC Buck converter [package=THT]
  Grove2 = TM1637 7segment 4digit display
  Grove3 = TM1637 7segment 4digit display
  IC1 = Hex Inverter Schmitt Trigger SN74HC14 [package="DIP (Dual Inline)"]
  LLC2 = Logic Level Converter [package="Breakout board"]
  LLC3 = Logic Level Converter [package="Breakout board"]
  J3 = STARBOARD_GND [package=starboard_ground_wide]
  R1 = Resistor [tolerance=±5% resistance=220 package=THT]
  Power_plug1 = Power plug
  C1 = Capacitor Polarized [package=cpol-radial-10uf-25v]
  A2 = MH-ET Live Minikit for ESP32
  Компонент5 = USB Mini-B Breakout [part_number=1764]  # not connected
  R3 = Resistor [tolerance=±5% resistance=220 package=THT]
  S5 = Taiway 100-SP-X-T1 SPDT Miniature Toggle Switch [part_number=100-SP-X-T1-0-0-B1-M1 package=THT]  # not connected
  R4 = Resistor [tolerance=±5% resistance=220 package=THT]
  J4 = Piezo Speaker  # not connected
  R5 = Resistor [tolerance=±5% resistance=220 package=THT]
  R6 = Resistor [tolerance=±5% resistance=220 package=THT]
  R7 = Resistor [tolerance=±5% resistance=220 package=THT]
  U2 = Optocoupler [package=THT]
  R8 = Resistor [tolerance=±5% resistance=220 package=THT]
  R9 = Resistor [tolerance=±5% resistance=220 package=THT]  # not connected

nets:
  VCC: Grove1.Vcc, U1.OUT+, Grove3.Vcc, LLC2.HV, C1.+
  N1: Grove1.GND, LLC2.H-GND
  N2: Grove1.DIO, LLC2.HV3
  N3: Grove1.CLK, LLC2.HV4
  N4: Компонент2.D+, U2.Pin_2
  N5: Компонент2.D-, R8.Pin_1
  N6: Matrix_keypad1.col1, M1.O7
  N7: Matrix_keypad1.col2, M1.O6
  N8: Matrix_keypad1.col3, M1.O5
  N9: Matrix_keypad1.col4, M1.O4
  N10: Matrix_keypad1.row1, M1.O3
  N11: Matrix_keypad1.row2, M1.O2
  N12: Matrix_keypad1.row3, M1.O1
  N13: Matrix_keypad1.row4, M1.O0
  VCC_2: M1.VCC, A2.3.3V
  N14: M1.SDA, A2.IO21
  N15: M1.SCL, A2.IO22
  N16: S2.COM, A2.IO16, R3.Pin_1
  N17: S4.leg0, Power_plug1.VCC
  N18: S4.leg1, U1.IN+
  N19: U1.IN-, Power_plug1.GND
  N20: Grove2.Vcc, LLC3.HV
  N21: Grove2.GND, LLC3.H-GND
  N22: Grove2.DIO, LLC3.HV3
  N23: Grove2.CLK, LLC3.HV4
  N24: Grove3.GND, J3.MOUNT
  N25: Grove3.CLK, LLC3.HV2
  N26: IC1.1A, R1.Pin_1
  N27: IC1.1Y, A2.IO35
  N28: IC1.2A, R5.Pin_1
  N29: IC1.2Y, A2.IO17
  N30: IC1.5Y, A2.IO26
  N31: IC1.5A, R6.Pin_1
  N32: IC1.6Y, A2.IO33
  N33: IC1.6A, R7.Pin_1
  N34: LLC2.LV, LLC3.LV
  N35: LLC2.L-GND, LLC3.L-GND
  N36: LLC2.LV3, A2.IO23
  N37: LLC2.LV4, A2.IO5
  N38: LLC3.LV1, A2.IO27
  N39: LLC3.LV2, A2.IO25
  N40: LLC3.LV3, A2.IO18
  N41: LLC3.LV4, A2.IO19
  N42: A2.SVN, U2.Pin_5
  N43: A2.IO34, R4.Pin_1

notes:
  +5V
  Gnd
  +3V3
  L-CLK
  R-DIO
  X
  Z
  T
  47 Ohm

custom parts:
  USB Mini-B Breakout: Simple but effective - this breakout board has a USB Mini-B connector, with all 5 pins broken out. Great for pairing with a microcontroller with USB support, or adding USB 5V power to a project.
  KEYPAD 4x4: Matrix keypad 16 buttons, 4 rows x 4 columns
  pcf8574 io expansion board: pcf8574 io expansion board.
  Mini-360 DC-DC Buck converter: Mini-360 DC-DC Buck converter. Tiny buck step down voltage converter, input voltage 4.75 to 23V output 1 to 17V adjustable. Available from ebay and the like.
  Logic Level Converter: 5V to/from 3.3V logic level converter
  MH-ET Live Minikit for ESP32: MH-ET Live Minikit for ESP32 ( http://mh.nodebb.com/topic/8/mh-et-live-minikit-for-esp32/2/) PCB footprint is invalid.
